# Fritzing sketch Alan_prot_01 (saved by Fritzing 0.9.3b)
breadboards: 3

parts:
  MUX1 = 74HC4051 [package="DIP (Dual Inline) [THT]"]  # not connected
  Q1 = Basic FET N-Channel [package="TO220 [THT]"]
  Q2 = Basic FET N-Channel [package="TO220 [THT]"]
  Q3 = Basic FET N-Channel [package="TO220 [THT]"]
  R1 = Resistor [tolerance=±5% resistance=1k package=THT]
  R2 = Resistor [tolerance=±5% resistance=1k package=THT]
  R3 = Resistor [tolerance=±5% resistance=1k package=THT]
  BATT-A = 18650 battery holder [package=battery-18650-kit]
  BATT-B = 18650 battery holder [package=battery-18650-kit]
  SR1 = 74HC595 [package="DIP16 [THT]"]
  U2 = SWITCH_SPDT [package=kps-1290]
  U3 = SWITCH_SPDT [package=kps-1290]
  ESP32_LORA = IC, DIP package, 36 pins [chip_label=ESP32]
  SR2 = 74HC595 [package="DIP16 [THT]"]
  C1 = Ceramic Capacitor [capacitance=100nF package="100 mil [THT, multilayer]"]
  C2 = Ceramic Capacitor [capacitance=100nF package="100 mil [THT, multilayer]"]

nets:
  N1: Q1.gate, R1.Pin_1
  GND: Q1.source, SR1.GND, SR1.OE, SR2.GND, SR2.OE, C1.0, C2.0
  N2: Q2.gate, R2.Pin_1
  N3: Q3.gate, R3.Pin_1
  m01: R1.Pin_0, SR1.Q0
  N4: BATT-A.+, U3.P
  N5: BATT-A.-, BATT-B.-
  N6: BATT-B.+, U2.P
  m02: SR1.Q1
  m03: SR1.Q2
  m04: SR1.Q3
  m05: SR1.Q4
  m06: SR1.Q5
  m07: SR1.Q6
  m08: SR1.Q7
  N7: SR1.Q7', SR2.DS
  3.3V: SR1.MR, SR1.VCC, SR2.MR, SR2.VCC, C1.1, C2.1
  sr_clock: SR1.SH_CP, ESP32_LORA.pin20, SR2.SH_CP
  sr_latch: SR1.ST_CP, ESP32_LORA.pin21, SR2.ST_CP
  sr_data: SR1.DS, ESP32_LORA.pin19
  m10: SR2.Q1
  m11: SR2.Q2
  m12: SR2.Q3
  m13: SR2.Q4
  m14: SR2.Q5
  m15: SR2.Q6
  m16: SR2.Q7
  m09: SR2.Q0

notes:
  Shift Registers

custom parts:
  74HC4051: 8 channel analog multiplexer/demultiplexer
  18650 battery holder: 18650 Battery Holder
